# Fritzing sketch 20140320-1 (Fritzing Wiring Diagram) (saved by Fritzing 0.8.7b)
breadboards: 1

parts:
  GPS1 = Adafruit Ultimate GPS Breakout
  Part1 = Compass Module - HMC6352
  Part2 = Arduino Uno (Rev3)

nets:
  N1: GPS1.TX, Part2.D5_PWM
  N2: GPS1.RX, Part2.D3_PWM
  GND: GPS1.GND, Part1.GND, Part2.GND
  VIN: GPS1.VIN, Part2.5V
  VCC: Part1.VCC, Part2.3V3
  N3: Part1.SDA, Part2.A4/SDA
  N4: Part1.SCL, Part2.A5/SCL
